# Fritzing sketch Sniffer (saved by Fritzing 1.0.5)
breadboards: 2

parts:
  MH-ET_LIVE_ESP32_DEVKIT1 = MH-ET LIVE ESP32 DEVKIT 38 pins
  U1 = mystery part, 13 pins [chip_label=Clock]
  Power_plug1 = Power plug
  U2 = mystery part, 6 pins [chip_label=SDCARD]
  R1 = Resistor [tolerance=±5% power=0.25W resistance=1k package=THT]
  R2 = Resistor [tolerance=±5% power=0.25W resistance=1k package=THT]
  R3 = Resistor [tolerance=±5% power=0.25W resistance=1k package=THT]
  R4 = Resistor [tolerance=±5% power=0.25W resistance=1k package=THT]
  R5 = Resistor [tolerance=±5% power=0.25W resistance=1k package=THT]
  R6 = Resistor [tolerance=±5% power=0.25W resistance=1k package=THT]
  R7 = Resistor [tolerance=±5% power=0.25W resistance=1k package=THT]
  R8 = Resistor [tolerance=±5% power=0.25W resistance=1k package=THT]
  Q1 = 2N7000 FET N-Channel [part_number=2N7000 package=TO92]
  Q2 = 2N7000 FET N-Channel [part_number=2N7000 package=TO92]
  Q3 = 2N7000 FET N-Channel [part_number=2N7000 package=TO92]
  Q4 = 2N7000 FET N-Channel [part_number=2N7000 package=TO92]
  LED1 = RGB LED (com. cathode, rgb) [color="Red (633nm)" current=0.030A package="5 mm [THT]"]
  R9 = Resistor [tolerance=±5% power=0.25W resistance=330 package=THT]

nets:
  3.3V: MH-ET_LIVE_ESP32_DEVKIT1.3V3, Power_plug1.VCC, U2.pin2, R2.Pin_1, R4.Pin_1, R6.Pin_1, R8.Pin_1
  N1: MH-ET_LIVE_ESP32_DEVKIT1.SVP, R8.Pin_0, Q4.drain
  N2: MH-ET_LIVE_ESP32_DEVKIT1.SVN, R6.Pin_0, Q3.drain
  N3: MH-ET_LIVE_ESP32_DEVKIT1.IO34, R4.Pin_0, Q2.drain
  N4: MH-ET_LIVE_ESP32_DEVKIT1.IO35, R2.Pin_0, Q1.drain
  N5: MH-ET_LIVE_ESP32_DEVKIT1.IO32, LED1.red_anode
  N6: MH-ET_LIVE_ESP32_DEVKIT1.IO33, R9.Pin_1
  N7: MH-ET_LIVE_ESP32_DEVKIT1.IO25, LED1.blue_anode
  GND: MH-ET_LIVE_ESP32_DEVKIT1.GND#64, U1.pin5, Power_plug1.GND, U2.pin1, LED1.common_cathode
  N8: MH-ET_LIVE_ESP32_DEVKIT1.IO23, U2.pin4
  N9: MH-ET_LIVE_ESP32_DEVKIT1.IO19, U2.pin3
  N10: MH-ET_LIVE_ESP32_DEVKIT1.IO18, U2.pin5
  N11: MH-ET_LIVE_ESP32_DEVKIT1.IO17, U2.pin6
  1.5V: U1.pin4, R1.Pin_0, R3.Pin_0, R5.Pin_0, R7.Pin_0, Q1.gate, Q2.gate, Q3.gate, Q4.gate
  N12: U1.pin8, R1.Pin_1, Q1.source
  N13: U1.pin9, R3.Pin_1, Q2.source
  N14: U1.pin10, R5.Pin_1, Q3.source
  N15: U1.pin13, R7.Pin_1, Q4.source
  N16: LED1.green_anode, R9.Pin_0

notes:
  Clock Voltage: 1V5
  ESP32 Voltage: 3V3

custom parts:
  MH-ET LIVE ESP32 DEVKIT 38 pins: http://mh.nodebb.com/topic/2/mh-et-live-esp32-devkit
  2N7000 FET N-Channel: A 2N7000 MOSFET N-Channel Transistor
