# Fritzing sketch ATtiny1616Boilerplate (saved by Fritzing 1.0.5)
breadboards: 1

parts:
  Composant1 = SO20W [chip_label=ATtiny1616 package=SO(w)]
  C1 = Ceramic Capacitor [capacitance=100nF voltage=35V package="100 mil [THT, multilayer]"]
  USBTTL1 = USB TTL Serial Cable
  LED1 = LED - 5mm [color="Red (633nm)" current=0.030A package="5 mm [THT]"]
  R1 = Resistor [tolerance=±5% power=0.25W resistance=470 package=THT]
  D1 = Rectifier Diode [part_number=1N5819 package="300 mil [THT]"]
  R2 = Resistor [tolerance=±5% power=0.25W resistance=100 package=THT]

nets:
  5V: Composant1.1, C1.0, USBTTL1.5V
  N1: Composant1.16, R2.Pin_0
  N2: Composant1.17, LED1.anode
  GND: Composant1.20, C1.1, USBTTL1.GND, R1.Pin_1
  N3: USBTTL1.RX, D1.anode
  N4: USBTTL1.TX, D1.cathode, R2.Pin_1
  N5: LED1.cathode, R1.Pin_0

notes:
  RX: Yellow
  TX: Orange (mine is White)
  If you use external power supply, disconnect VCC
  but keep GND connected (common reference)
  CTS (Brown) and RTS (Green) are not used
  If you use a schottky diode, the 100Ω resistor doesn't seem needed at all
  If you don't have a schottky diode, replace with a 4.7kΩ resistor, but expect complications
  or 3.3V
  If you don't have a schottky diode,
  replace with a 4.7kΩ resistor, but expect complications
  I have better results without any resistor
  at all when using a schottky diode
  MANDATORY capacitor. Place as close as possible to ATtiny
