# Fritzing sketch DRV8833 (saved by Fritzing 1.0.5)
breadboards: 1

parts:
  IC1 = DRV8833 Motor Driver Board (MJKDZ) [package="DIP (Dual Inline) [THT]"]
  MH-ET_LIVE_ESP32_DEVKIT1 = MH-ET LIVE ESP32 DEVKIT 38 pins
  U1 = mystery part, 4 pins [chip_label=Clock]
  R1 = Resistor [tolerance=±5% power=0.25W resistance=470 package=THT]
  R2 = Resistor [tolerance=±5% power=0.25W resistance=470 package=THT]
  C2 = Ceramic Capacitor [capacitance=100nF voltage=35V package="100 mil [THT, multilayer]"]
  C1 = Ceramic Capacitor [capacitance=100nF voltage=35V package="100 mil [THT, multilayer]"]

nets:
  N1: IC1.pin1, MH-ET_LIVE_ESP32_DEVKIT1.IO32
  N2: IC1.pin2, MH-ET_LIVE_ESP32_DEVKIT1.IO33
  GND: IC1.pin3, MH-ET_LIVE_ESP32_DEVKIT1.GND
  3.3V: IC1.pin4, MH-ET_LIVE_ESP32_DEVKIT1.3V3
  N3: IC1.pin5, MH-ET_LIVE_ESP32_DEVKIT1.IO26
  N4: IC1.pin6, MH-ET_LIVE_ESP32_DEVKIT1.IO27
  N5: IC1.pin8, U1.pin3, C2.1
  N6: IC1.pin9, R2.Pin_1
  N7: IC1.pin10, R1.Pin_0
  N8: IC1.pin11, U1.pin2, C1.0
  N9: U1.pin1, R1.Pin_1, C1.1
  N10: U1.pin4, R2.Pin_0, C2.0

notes:
  J2 Shorted, or put EEP to VCC
  Capacitors did not prove to be necessary (100pF~100nF)
  Connect EEP to VCC if J2 is not shorted

custom parts:
  DRV8833 Motor Driver Board (MJKDZ): A module made by MJKDZ, containg DRV8833 motor driver chip on PCB with 12-pin DIP 600mil footprint. Contains decoupling caps and an enable pad (J2). Does not bring out all IC pins. EEP = SLEEP input (needs pulling logic high to enable motors) ULT = FAULT output.
  MH-ET LIVE ESP32 DEVKIT 38 pins: http://mh.nodebb.com/topic/2/mh-et-live-esp32-devkit
