# Fritzing sketch Sniffer (saved by Fritzing 1.0.5)
breadboards: 2

parts:
  MH-ET_LIVE_ESP32_DEVKIT1 = MH-ET LIVE ESP32 DEVKIT 38 pins
  Power_plug1 = Power plug
  U2 = mystery part, 6 pins [chip_label=SDCARD]
  LED1 = RGB LED (com. cathode, rgb) [color="Red (633nm)" current=0.030A package="5 mm [THT]"]
  R9 = Resistor [tolerance=±5% power=0.25W resistance=330 package=THT]
  U1 = mystery part, 14 pins [chip_label=Clock]
  LM339N = LM339 [chip_label=LM339 package="DIP (Dual Inline) [THT]"]
  LM339N_PWR = LM339 [package="DIP (Dual Inline) [THT]"]
  LM339N_A = LM339 [package="DIP (Dual Inline) [THT]"]
  LM339N_B = LM339 [package="DIP (Dual Inline) [THT]"]
  LM339N_C = LM339 [package="DIP (Dual Inline) [THT]"]
  LM339N_D = LM339 [package="DIP (Dual Inline) [THT]"]
  R10 = Resistor [tolerance=±5% power=0.25W resistance=47k package=THT]
  R11 = Resistor [tolerance=±5% power=0.25W resistance=100k package=THT]
  R12 = Resistor [tolerance=±5% power=0.25W resistance=10k package=THT]
  R13 = Resistor [tolerance=±5% power=0.25W resistance=10k package=THT]
  R14 = Resistor [tolerance=±5% power=0.25W resistance=10k package=THT]
  R15 = Resistor [tolerance=±5% power=0.25W resistance=10k package=THT]

nets:
  3.3V: MH-ET_LIVE_ESP32_DEVKIT1.3V3, Power_plug1.VCC, U2.pin2, LM339N.connector2, LM339N_PWR.pin3, R12.Pin_0, R13.Pin_0, R14.Pin_0, R15.Pin_0
  N1: MH-ET_LIVE_ESP32_DEVKIT1.SVP, LM339N.connector12, LM339N_D.pin13, R12.Pin_1
  N2: MH-ET_LIVE_ESP32_DEVKIT1.SVN, LM339N.connector13, LM339N_C.pin14, R13.Pin_1
  N3: MH-ET_LIVE_ESP32_DEVKIT1.IO34, LM339N.connector1, LM339N_B.pin2, R14.Pin_1
  N4: MH-ET_LIVE_ESP32_DEVKIT1.IO35, LM339N.connector0, LM339N_A.pin1, R15.Pin_1
  N5: MH-ET_LIVE_ESP32_DEVKIT1.IO32, LED1.red_anode
  N6: MH-ET_LIVE_ESP32_DEVKIT1.IO33, R9.Pin_1
  N7: MH-ET_LIVE_ESP32_DEVKIT1.IO25, LED1.blue_anode
  GND: MH-ET_LIVE_ESP32_DEVKIT1.GND#64, Power_plug1.GND, U2.pin1, LED1.common_cathode, U1.pin5, LM339N.connector11, LM339N_PWR.pin12, R11.Pin_1
  N8: MH-ET_LIVE_ESP32_DEVKIT1.IO23, U2.pin4
  N9: MH-ET_LIVE_ESP32_DEVKIT1.IO19, U2.pin3
  N10: MH-ET_LIVE_ESP32_DEVKIT1.IO18, U2.pin5
  N11: MH-ET_LIVE_ESP32_DEVKIT1.IO17, U2.pin6
  N12: LED1.green_anode, R9.Pin_0
  1.5V: U1.pin4, R10.Pin_0
  N13: U1.pin8, LM339N.connector6, LM339N_A.pin7
  N14: U1.pin10, LM339N.connector8, LM339N_C.pin9
  N15: U1.pin13, LM339N.connector10, LM339N_D.pin11
  N16: U1.pin14, LM339N.connector4, LM339N_B.pin5
  N17: LM339N.connector3, LM339N.connector5, LM339N.connector7, LM339N.connector9, LM339N_A.pin6, LM339N_B.pin4, LM339N_C.pin8, LM339N_D.pin10, R10.Pin_1, R11.Pin_0

notes:
  Clock Voltage: 1V5
  ESP32 Voltage: 3V3

custom parts:
  MH-ET LIVE ESP32 DEVKIT 38 pins: http://mh.nodebb.com/topic/2/mh-et-live-esp32-devkit
  LM339: A Quad Norton Op AMp
  LM339: A Quad Norton Op AMp
  LM339: A Quad Norton Op AMp
  LM339: A Quad Norton Op AMp
  LM339: A Quad Norton Op AMp
  LM339: A Quad Norton Op AMp
